// Logisim project CalculadoraRealOficialDeVerdade.circ as structural Verilog: 7 circuits, main circuit main
module main (
  input  _1___Somar,
  input  in_2,
  input  [6:0] in_3,
  input  in_4,
  input  [6:0] in_5,
  input  in_6,
  output [6:0] out_7
);

  wire c2_1_msb, c2_1_s1, c2_1_s2, c2_1_s3, c2_1_s4, c2_1_s5, c2_1_s6, c2_2_msb, c2_2_s1, c2_2_s2, c2_2_s3,
       c2_2_s4, c2_2_s5, c2_2_s6, MSB, Overflow, somasubtracao_1_msb, somasubtracao_1_s1, somasubtracao_1_s2,
       somasubtracao_1_s3, somasubtracao_1_s4, somasubtracao_1_s5, somasubtracao_1_s6, xor_1_out;

  _7_Segment_Display u_7_segment_display_1 (.g(in_3[6]));  // open: f, a, b, e, d, c, dp
  Hex_Digit_Display hex_digit_display_1 (.value({{2{in_2}}, in_3[5:4]}));  // open: dp
  Hex_Digit_Display hex_digit_display_2 (.value(in_3[3:0]));  // open: dp
  _7_Segment_Display #(.decimalPoint("false")) u_7_segment_display_2 (.g(1'b1));  // open: f, a, b, e, d, c
  _7_Segment_Display #(.decimalPoint("false")) u_7_segment_display_3 (
    .g(1'b1), .f(_1___Somar), .e(_1___Somar));  // open: a, b, d, c
  C2 c2_1 (
    .e1(in_3[0]), .e2(in_3[1]), .e3(in_3[2]), .e4(in_3[3]), .e5(in_3[4]), .e6(in_3[5]), .e7(in_3[6]),
    .NEGATIVO(in_3[6]), .s1(c2_1_s1), .s2(c2_1_s2), .s3(c2_1_s3), .s4(c2_1_s4), .s5(c2_1_s5), .s6(c2_1_s6),
    .msb(c2_1_msb));
  C2 c2_2 (
    .e1(in_5[0]), .e2(in_5[1]), .e3(in_5[2]), .e4(in_5[3]), .e5(in_5[4]), .e6(in_5[5]), .e7(in_5[6]),
    .NEGATIVO(in_5[6]), .s1(c2_2_s1), .s2(c2_2_s2), .s3(c2_2_s3), .s4(c2_2_s4), .s5(c2_2_s5), .s6(c2_2_s6),
    .msb(c2_2_msb));
  _7_Segment_Display u_7_segment_display_4 (.g(in_5[6]));  // open: f, a, b, e, d, c, dp
  Hex_Digit_Display hex_digit_display_3 (.value({{2{in_4}}, in_5[5:4]}));  // open: dp
  Hex_Digit_Display hex_digit_display_4 (.value(in_5[3:0]));  // open: dp
  LED led_1 (.in(Overflow));
  _7_Segment_Display u_7_segment_display_5 (.g(MSB));  // open: f, a, b, e, d, c, dp
  SomaSubtracao somasubtracao_1 (
    .A1(c2_1_s1), .A2(c2_1_s2), .A3(c2_1_s3), .A4(c2_1_s4), .A5(c2_1_s5), .A6(c2_1_s6), .MSBA(c2_1_msb),
    .B1(c2_2_s1), .B2(c2_2_s2), .B3(c2_2_s3), .B4(c2_2_s4), .B5(c2_2_s5), .B6(c2_2_s6), .MSBB(c2_2_msb),
    .SomaOuSub(_1___Somar), .S1(somasubtracao_1_s1), .S2(somasubtracao_1_s2), .S3(somasubtracao_1_s3),
    .S4(somasubtracao_1_s4), .S5(somasubtracao_1_s5), .S6(somasubtracao_1_s6), .MSB(somasubtracao_1_msb),
    .OverFlow(Overflow));
  xor xor_1 (xor_1_out, in_3[6], in_5[6]);
  Hex_Digit_Display hex_digit_display_5 (.value({{2{in_6}}, out_7[5:4]}));  // open: dp
  Hex_Digit_Display hex_digit_display_6 (.value(out_7[3:0]));  // open: dp
  xor xor_2 (MSB, somasubtracao_1_msb, xor_1_out);
  C2 c2_3 (
    .e1(somasubtracao_1_s1), .e2(somasubtracao_1_s2), .e3(somasubtracao_1_s3), .e4(somasubtracao_1_s4),
    .e5(somasubtracao_1_s5), .e6(somasubtracao_1_s6), .e7(somasubtracao_1_msb), .NEGATIVO(MSB),
    .s1(out_7[0]), .s2(out_7[1]), .s3(out_7[2]), .s4(out_7[3]), .s5(out_7[4]), .s6(out_7[5]), .msb(out_7[6]));

  // Other names for the same wires on the sheet: Botao1 = _1___Somar; dig1R[3:0] = out_7[3:0];
  //   dig2A[3:0] = {{2{in_2}}, in_3[5:4]}; dig2B[3:0] = {{2{in_4}}, in_5[5:4]}; dig2R[3:0] = {{2{in_6}}, out_7[5:4]};
  //   dig1A[3:0] = in_3[3:0]; sinA = in_3[6]; dig1B[3:0] = in_5[3:0]; sinB = in_5[6]

  // Notes on the sheet:
  //   A
  //   B
  //   0 - Subtrair
  //   =
  //   Saída em binário
endmodule

module meioSomador (
  input  A,
  input  B,
  output S,
  output CarryOUT
);

  xor xor_1 (S, A, B);
  and and_1 (CarryOUT, A, B);
endmodule

module Somador (
  input  CarryIN,
  input  A,
  input  B,
  output S,
  output CarryOUT
);

  wire and_1_out, and_2_out, and_3_out, xor_1_out;

  and and_1 (and_1_out, CarryIN, A);
  and and_2 (and_2_out, CarryIN, B);
  and and_3 (and_3_out, A, B);
  xor xor_1 (xor_1_out, CarryIN, A);
  xor xor_2 (S, xor_1_out, B);
  or or_1 (CarryOUT, and_1_out, and_2_out, and_3_out);
endmodule

module SomaSubtracao (
  input  A1,
  input  A2,
  input  A3,
  input  A4,
  input  A5,
  input  A6,
  input  MSBA,
  input  B1,
  input  B2,
  input  B3,
  input  B4,
  input  B5,
  input  B6,
  input  MSBB,
  input  SomaOuSub,
  output S1,
  output S2,
  output S3,
  output S4,
  output S5,
  output S6,
  output MSB,
  output OverFlow
);

  wire meiosomador_1_carryout, meiosubtrator_1_carryout, MSBsoma, MSBsub, not_1_out, OverflowSOMA,
       OverflowSUB, soma1, soma2, soma3, soma4, soma5, soma6, somador_1_carryout, somador_2_carryout,
       somador_3_carryout, somador_4_carryout, somador_5_carryout, somador_6_carryout, sub1, sub2, sub3,
       sub4, sub5, sub6, subtrator_1_carryout, subtrator_2_carryout, subtrator_3_carryout,
       subtrator_4_carryout, subtrator_5_carryout, subtrator_6_carryout;
  wire [7:0] RSoma, RSub;

  not not_1 (not_1_out, SomaOuSub);
  and and_1 (soma1, SomaOuSub, RSoma[0]);
  and and_2 (soma2, SomaOuSub, RSoma[1]);
  and and_3 (soma3, SomaOuSub, RSoma[2]);
  and and_4 (soma4, SomaOuSub, RSoma[3]);
  and and_5 (sub1, not_1_out, RSub[0]);
  and and_6 (sub2, not_1_out, RSub[1]);
  and and_7 (sub3, not_1_out, RSub[2]);
  and and_8 (sub4, not_1_out, RSub[3]);
  meioSomador meiosomador_1 (.A(A1), .B(B1), .S(RSoma[0]), .CarryOUT(meiosomador_1_carryout));
  Somador somador_1 (.CarryIN(meiosomador_1_carryout), .A(A2), .B(B2), .S(RSoma[1]), .CarryOUT(somador_1_carryout));
  Somador somador_2 (.CarryIN(somador_1_carryout), .A(A3), .B(B3), .S(RSoma[2]), .CarryOUT(somador_2_carryout));
  Somador somador_3 (.CarryIN(somador_2_carryout), .A(A4), .B(B4), .S(RSoma[3]), .CarryOUT(somador_3_carryout));
  Somador somador_4 (.CarryIN(somador_3_carryout), .A(A5), .B(B5), .S(RSoma[4]), .CarryOUT(somador_4_carryout));
  Somador somador_5 (.CarryIN(somador_4_carryout), .A(A6), .B(B6), .S(RSoma[5]), .CarryOUT(somador_5_carryout));
  Somador somador_6 (.CarryIN(somador_5_carryout), .A(MSBA), .B(MSBB), .S(RSoma[6]), .CarryOUT(somador_6_carryout));
  xor xor_1 (RSoma[7], somador_5_carryout, somador_6_carryout);
  and and_9 (sub5, not_1_out, RSub[4]);
  and and_10 (sub6, not_1_out, RSub[5]);
  and and_11 (MSBsub, not_1_out, RSub[6]);
  and and_12 (OverflowSUB, not_1_out, RSub[7]);
  and and_13 (soma5, SomaOuSub, RSoma[4]);
  and and_14 (soma6, SomaOuSub, RSoma[5]);
  and and_15 (MSBsoma, SomaOuSub, RSoma[6]);
  and and_16 (OverflowSOMA, SomaOuSub, RSoma[7]);
  meioSubtrator meiosubtrator_1 (.A(A1), .B(B1), .S(RSub[0]), .CarryOUT(meiosubtrator_1_carryout));
  Subtrator subtrator_1 (
    .CarryIN(meiosubtrator_1_carryout), .A(A2), .B(B2), .S(RSub[1]), .CarryOUT(subtrator_1_carryout));
  Subtrator subtrator_2 (.CarryIN(subtrator_1_carryout), .A(A3), .B(B3), .S(RSub[2]), .CarryOUT(subtrator_2_carryout));
  Subtrator subtrator_3 (.CarryIN(subtrator_2_carryout), .A(A4), .B(B4), .S(RSub[3]), .CarryOUT(subtrator_3_carryout));
  Subtrator subtrator_4 (.CarryIN(subtrator_3_carryout), .A(A5), .B(B5), .S(RSub[4]), .CarryOUT(subtrator_4_carryout));
  Subtrator subtrator_5 (.CarryIN(subtrator_4_carryout), .A(A6), .B(B6), .S(RSub[5]), .CarryOUT(subtrator_5_carryout));
  Subtrator subtrator_6 (
    .CarryIN(subtrator_5_carryout), .A(MSBA), .B(MSBB), .S(RSub[6]), .CarryOUT(subtrator_6_carryout));
  or or_1 (S1, soma1, sub1);
  or or_2 (S2, soma2, sub2);
  or or_3 (S3, soma3, sub3);
  or or_4 (S4, soma4, sub4);
  or or_5 (S5, soma5, sub5);
  or or_6 (S6, soma6, sub6);
  or or_7 (MSB, MSBsoma, MSBsub);
  or or_8 (OverFlow, OverflowSOMA, OverflowSUB);
  xor xor_2 (RSub[7], subtrator_5_carryout, subtrator_6_carryout);

  // Other names for the same wires on the sheet: a7 = MSBA; b7 = MSBB
endmodule

module meioSubtrator (
  input  A,
  input  B,
  output S,
  output CarryOUT
);

  wire not_1_out;

  not not_1 (not_1_out, A);
  xor xor_1 (S, A, B);
  and and_1 (CarryOUT, not_1_out, B);
endmodule

module Subtrator (
  input  CarryIN,
  input  A,
  input  B,
  output S,
  output CarryOUT
);

  wire and_1_out, and_2_out, and_3_out, not_1_out, not_2_out, xor_1_out;

  not not_1 (not_1_out, A);
  not not_2 (not_2_out, A);
  xor xor_1 (xor_1_out, CarryIN, A);
  xor xor_2 (S, xor_1_out, B);
  and and_1 (and_1_out, CarryIN, not_1_out);
  and and_2 (and_2_out, CarryIN, B);
  or or_1 (CarryOUT, and_1_out, and_2_out, and_3_out);
  and and_3 (and_3_out, not_2_out, B);
endmodule

module C2 (
  input  e1,
  input  e2,
  input  e3,
  input  e4,
  input  e5,
  input  e6,
  input  e7,
  input  NEGATIVO,
  output s1,
  output s2,
  output s3,
  output s4,
  output s5,
  output s6,
  output msb
);

  wire xor_1_out, xor_2_out, xor_3_out, xor_4_out, xor_5_out, xor_6_out, xor_7_out;

  xor xor_1 (xor_1_out, e1, NEGATIVO);
  xor xor_2 (xor_2_out, e2, NEGATIVO);
  xor xor_3 (xor_3_out, e3, NEGATIVO);
  xor xor_4 (xor_4_out, e4, NEGATIVO);
  xor xor_5 (xor_5_out, e5, NEGATIVO);
  xor xor_6 (xor_6_out, e6, NEGATIVO);
  xor xor_7 (xor_7_out, e7, NEGATIVO);
  SomaSubtracao somasubtracao_1 (
    .A1(xor_1_out), .A2(xor_2_out), .A3(xor_3_out), .A4(xor_4_out), .A5(xor_5_out), .A6(xor_6_out),
    .MSBA(xor_7_out), .B1(NEGATIVO), .SomaOuSub(1'b1), .S1(s1), .S2(s2), .S3(s3), .S4(s4), .S5(s5), .S6(s6),
    .MSB(msb));  // open: B2, B3, B4, B5, B6, MSBB, OverFlow
endmodule
